# Fritzing sketch mods (saved by Fritzing 0.9.3b)
breadboards: 1

parts:
  U2 = attiny85 [package=dip]
  BAT1 = Battery Holders [package=battcon_245mm_pth]
  LED1 = RGB LED (com. cathode, rgb) [package="5 mm [THT]"]
  S1 = Pushbutton [package="[SMD]"]
  R6 = Resistor [tolerance=±5% resistance=220 package="1206 [SMD]"]
  LED3 = RGB LED (com. cathode, rgb) [package="5 mm [THT]"]
  LED4 = RGB LED (com. cathode, rgb) [package="5 mm [THT]"]
  R1 = Resistor [tolerance=±5% resistance=220 package="1206 [SMD]"]
  R5 = Resistor [tolerance=±5% resistance=220 package="1206 [SMD]"]
  R4 = Resistor [tolerance=±5% resistance=220 package="1206 [SMD]"]
  LED5 = RGB LED (com. cathode, rgb) [package="5 mm [THT]"]
  R2 = Resistor [tolerance=±5% resistance=220 package="1206 [SMD]"]
  LED2 = RGB LED (com. cathode, rgb) [package="5 mm [THT]"]

nets:
  N1: U2.Pin_1, LED1.red_anode, LED3.red_anode, LED4.red_anode, LED5.red_anode, LED2.red_anode
  N2: U2.Pin_2, LED5.green_anode, LED5.blue_anode
  N3: U2.Pin_3, LED4.green_anode, LED4.blue_anode
  N4: U2.Pin_4, BAT1.+, R6.Pin_0, R1.Pin_0, R5.Pin_0, R4.Pin_0, R2.Pin_0
  N5: U2.Pin_5, LED1.green_anode, LED1.blue_anode
  N6: U2.Pin_6, LED2.green_anode, LED2.blue_anode
  N7: U2.Pin_7, LED3.green_anode, LED3.blue_anode
  N8: U2.Pin_8, BAT1.-, S1.Pin_3, S1.Pin_4
  N9: LED1.common_cathode, R6.Pin_1
  N10: LED3.common_cathode, R4.Pin_1
  N11: LED4.common_cathode, R2.Pin_1
  N12: R1.Pin_1, LED5.common_cathode
  N13: R5.Pin_1, LED2.common_cathode
